# Fritzing sketch Schema (saved by Fritzing 0.9.3b)
breadboards: 2

parts:
  Part1 = Arduino Uno (Rev3)
  U3 = POT [package=pot_mammoth]
  J1 = Basic Servo

nets:
  N1: Part1.A5/SCL, U3.A
  N2: Part1.D3_PWM, J1.pulse
  5V: Part1.5V, U3.E, J1.vcc
  GND: Part1.GND, U3.S, J1.gnd
